# Fritzing sketch 1_light_led (saved by Fritzing 0.9.3b)
breadboards: 1

parts:
  Raspberry_Pi_1 = Raspberry Pi 3 [part_number=RPI-3-V1.2]
  R1 = Resistor [tolerance=±5% resistance=220 package="1206 [SMD]"]
  LED1 = smd LED [color="Red (633nm)" package="0805 [SMD]"]

nets:
  N1: Raspberry_Pi_1.GPIO18, LED1.cathode
  N2: Raspberry_Pi_1.GND, R1.Pin_1
  N3: R1.Pin_0, LED1.anode
