# Fritzing sketch 2_read_light (saved by Fritzing 0.9.3b)
breadboards: 1

parts:
  Raspberry_Pi_1 = Raspberry Pi 3 [part_number=RPI-3-V1.2]
  R1 = Resistor [tolerance=±5% resistance=220 package="1206 [SMD]"]
  R2 = Photocell (LDR) [package=THT]

nets:
  N1: Raspberry_Pi_1.GPIO18, R1.Pin_1, R2.pin_0
  N2: Raspberry_Pi_1.GND, R1.Pin_0
  N3: Raspberry_Pi_1.5V, R2.pin_1
