# Fritzing sketch 3_read_potentiometer (saved by Fritzing 0.9.3b)
breadboards: 1

parts:
  Raspberry_Pi_1 = Raspberry Pi 3 [part_number=RPI-3-V1.2]
  U1 = POT [package=pot_alpha_rv16af-20]

nets:
  N1: Raspberry_Pi_1.GPIO18, U1.S
  N2: Raspberry_Pi_1.GND, U1.A
  N3: Raspberry_Pi_1.5V, U1.E
