# Fritzing sketch 5_dim_nightlight (saved by Fritzing 0.9.3b)
breadboards: 1

parts:
  Raspberry_Pi_1 = Raspberry Pi 3 [part_number=RPI-3-V1.2]
  R1 = Resistor [tolerance=±5% resistance=220 package="1206 [SMD]"]
  R2 = Photocell (LDR) [package=THT]
  LED1 = LED - 5mm [color="Red (633nm)" package="5 mm [THT]"]
  R3 = Resistor [tolerance=±5% resistance=220 package=THT]
  U1 = POT [package=pot_alpha_rv16af-20]

nets:
  N1: Raspberry_Pi_1.GND, R1.Pin_0, R3.Pin_1, U1.E
  N2: Raspberry_Pi_1.GPIO23, U1.A
  N3: Raspberry_Pi_1.GPIO18, R1.Pin_1, R2.pin_0
  N4: Raspberry_Pi_1.5V, R2.pin_1
  N5: LED1.cathode, U1.S
  N6: LED1.anode, R3.Pin_0
