# Fritzing sketch simple_theremin (saved by Fritzing 0.9.3b)
breadboards: 1

parts:
  Raspberry_Pi_1 = Raspberry Pi 3 [part_number=RPI-3-V1.2]
  U2 = 4093 4 x 2 Input Schmitt Trigger NAND Gate, single part [part_number=4093 package="DIP (Dual Inline) [THT]"]
  R1 = PHOTOCELL [package=photocell]
  C1 = Capacitor Polarized [part_number=2.2 package=cpol-radial-10uf-25v]
  M1 = fc-51 [package=THT]
  J1 = Piezo Speaker

nets:
  GND: Raspberry_Pi_1.GND, U2.GND, C1.-, M1.pin2, J1.pin1
  5V: Raspberry_Pi_1.5V, U2.B3, U2.VDD, M1.pin3
  N1: U2.A1, R1.P$2, C1.+
  N2: U2.B1, U2.Q3
  N3: U2.Q1, R1.P$1, J1.pin2
  N4: U2.A3, M1.pin1
